# Fritzing sketch EducaInoV0.9 (saved by Fritzing 0.9.2b)
circuit board: 9.61856cm x 7.65745cm
breadboards: 1

parts:
  Arduino_nano1 = Arduino Nano (Rev3.0) (ICSP)
  L293D1 = L293D [package=THT]
  Sensor_ultrassonico1 = female pin header, 4 pins [form="♀ (female)"]
  Sensor_ultrassonico2 = female pin header, 4 pins [form="♀ (female)"]
  Sensor_ultrassonico4 = female pin header, 4 pins [form="♀ (female)"]
  Sensor_ultrassonico3 = female pin header, 4 pins [form="♀ (female)"]
  Motor_V+ = female pin header, 2 pins [form="♀ (female)"]
  Buzzer1 = Piezo Speaker
  R2 = Resistor [tolerance=±5% resistance=150 package=THT]
  Modulo_Bluetooh1 = female pin header, 4 pins [form="♀ (female)"]
  Rodas2 = female pin header, 2 pins [form="♀ (female)"]
  Rodas1 = female pin header, 2 pins [form="♀ (female)"]
  Arduino_V+1 = female pin header, 2 pins [form="♀ (female)"]
  Sensor_Outros = female pin header, 4 pins [form="♀ (female)"]

nets:
  N1: Arduino_nano1.D1/TX, Modulo_Bluetooh1.pin4
  N2: Arduino_nano1.D0/RX, Modulo_Bluetooh1.pin3
  N3: Arduino_nano1.GND, L293D1.0V, Sensor_ultrassonico1.pin4, Sensor_ultrassonico2.pin4, Sensor_ultrassonico4.pin4, Sensor_ultrassonico3.pin4, Motor_V+.pin2, Buzzer1.pin2, Modulo_Bluetooh1.pin1, Modulo_Bluetooh1.pin2, Arduino_V+1.pin2, Sensor_Outros.pin4
  N4: Arduino_nano1.D2, L293D1.In_4
  N5: Arduino_nano1.D3, L293D1.In_3
  N6: Arduino_nano1.D4, L293D1.In_2
  N7: Arduino_nano1.D5, L293D1.In_1
  N8: Arduino_nano1.D7, Sensor_Outros.pin1
  N9: Arduino_nano1.D8, Sensor_Outros.pin2
  N10: Arduino_nano1.D9, Sensor_ultrassonico4.pin1
  N11: Arduino_nano1.D10, Sensor_ultrassonico4.pin2
  N12: Arduino_nano1.D11/MOSI, Sensor_ultrassonico3.pin1
  N13: Arduino_nano1.D12/MISO, Sensor_ultrassonico3.pin2
  N14: Arduino_nano1.VIN, Arduino_V+1.pin1
  N15: Arduino_nano1.5V, L293D1.Enable_1, L293D1.Enable_2, L293D1.+V, Sensor_ultrassonico1.pin3, Sensor_ultrassonico2.pin3, Sensor_ultrassonico4.pin3, Sensor_ultrassonico3.pin3, Sensor_Outros.pin3
  N16: Arduino_nano1.A7, R2.Pin_0
  N17: Arduino_nano1.A0, Sensor_ultrassonico1.pin1
  N18: Arduino_nano1.AREF, Sensor_ultrassonico1.pin2
  N19: Arduino_nano1.3V3, Sensor_ultrassonico2.pin1
  N20: Arduino_nano1.D13/SCK, Sensor_ultrassonico2.pin2
  N21: L293D1.Out_1_(_Controlled_by_Enable_1_), Rodas2.pin1
  N22: L293D1.Out_2_(_Controlled_by_Enable_1_), Rodas2.pin2
  N23: L293D1.+Vmotor, Motor_V+.pin1
  N24: L293D1.Out_3_(_Controlled_by_Enable_2_), Rodas1.pin2
  N25: L293D1.Out_4_(_Controlled_by_Enable_2_), Rodas1.pin1
  N26: Buzzer1.pin1, R2.Pin_1
