# Fritzing sketch EducaInoV1 (saved by Fritzing 0.9.2b)
circuit board: 6.5cm x 6.5cm
breadboards: 1

parts:
  Arduino_nano2 = Arduino Nano (Rev3.0) (ICSP)
  L293D2 = L293D [package=THT]
  DIO1 = female pin header, 4 pins [form="♀ (female)"]
  DIO3 = female pin header, 4 pins [form="♀ (female)"]
  DIO4 = female pin header, 4 pins [form="♀ (female)"]
  DIO2 = female pin header, 4 pins [form="♀ (female)"]
  Motor_5V+ = female pin header, 2 pins [form="♀ (female)"]
  Buzzer2 = Piezo Speaker
  R1 = Resistor [tolerance=±5% resistance=150 package=THT]
  Bluetooh = female pin header, 4 pins [form="♀ (female)"]
  RodasB = female pin header, 2 pins [form="♀ (female)"]
  RodasA = female pin header, 2 pins [form="♀ (female)"]
  Arduino_9V+ = female pin header, 2 pins [form="♀ (female)"]
  Liga/Desliga = female pin header, 2 pins [form="♀ (female)"]
  I/O1 = female pin header, 3 pins [form="♀ (female)"]
  I/O2 = female pin header, 3 pins [form="♀ (female)"]
  I/O3 = female pin header, 3 pins [form="♀ (female)"]
  DIO5 = female pin header, 4 pins [form="♀ (female)"]

nets:
  N1: Arduino_nano2.D1/TX, Bluetooh.pin4
  N2: Arduino_nano2.D0/RX, Bluetooh.pin3
  N3: Arduino_nano2.GND, L293D2.0V, DIO1.pin4, DIO3.pin4, DIO4.pin4, DIO2.pin4, Motor_5V+.pin2, Buzzer2.pin2, Bluetooh.pin2, Arduino_9V+.pin2, I/O1.pin1, I/O2.pin1, I/O3.pin1, DIO5.pin4
  N4: Arduino_nano2.D2, L293D2.In_4
  N5: Arduino_nano2.D3, L293D2.Enable_2
  N6: Arduino_nano2.D4, L293D2.In_3
  N7: Arduino_nano2.D5, L293D2.In_2
  N8: Arduino_nano2.D6, L293D2.In_1
  N9: Arduino_nano2.D7, L293D2.Enable_1
  N10: Arduino_nano2.D8, I/O1.pin3
  N11: Arduino_nano2.D9, I/O2.pin3
  N12: Arduino_nano2.D10, I/O3.pin3
  N13: Arduino_nano2.D11/MOSI, DIO1.pin1
  N14: Arduino_nano2.D12/MISO, DIO1.pin2
  N15: Arduino_nano2.VIN, Arduino_9V+.pin1
  N16: Arduino_nano2.5V, L293D2.+V, DIO1.pin3, DIO3.pin3, DIO4.pin3, DIO2.pin3, Bluetooh.pin1, I/O1.pin2, I/O2.pin2, I/O3.pin2, DIO5.pin3
  N17: Arduino_nano2.A7, R1.Pin_0
  N18: Arduino_nano2.A6, DIO5.pin1
  N19: Arduino_nano2.A5, DIO5.pin2
  N20: Arduino_nano2.A4, DIO4.pin1
  N21: Arduino_nano2.A3, DIO4.pin2
  N22: Arduino_nano2.A2, DIO3.pin1
  N23: Arduino_nano2.A1, DIO3.pin2
  N24: Arduino_nano2.A0, DIO2.pin1
  N25: Arduino_nano2.D13/SCK, DIO2.pin2
  N26: L293D2.Out_1_(_Controlled_by_Enable_1_), RodasB.pin1
  N27: L293D2.Out_2_(_Controlled_by_Enable_1_), RodasB.pin2
  N28: L293D2.+Vmotor, Liga/Desliga.pin1
  N29: L293D2.Out_3_(_Controlled_by_Enable_2_), RodasA.pin2
  N30: L293D2.Out_4_(_Controlled_by_Enable_2_), RodasA.pin1
  N31: Motor_5V+.pin1, Liga/Desliga.pin2
  N32: Buzzer2.pin1, R1.Pin_1
